// Logisim project projeto1.circ as structural Verilog: 6 circuits, main circuit \-- somador de dois bits
module ULA (
  input  [7:0] A,
  input  [7:0] B,
  input  [1:0] S,
  output [7:0] R,
  output o0,
  output o1,
  output o2,
  output o3
);

  wire soma_1_o0, \subtração_1_o0 ;
  wire [7:0] soma_1_s, \subtração_1_s ;

  \Subtração  \subtração_1  (.S(\subtração_1_s ), .o0(\subtração_1_o0 ), .A(A), .B(B));
  Comparador comparador_1 (.A(A), .o3(o3), .o2(o2), .o1(o1));
  Soma soma_1 (.A(B), .S(soma_1_s), .o0(soma_1_o0), .B(A));
  Multiplexer #(.select(2), .width(8)) multiplexer_1 (
    .in0(soma_1_s), .in1(\subtração_1_s ), .out(R), .sel(S));  // open: in2, in3, en
  Multiplexer #(.select(2)) multiplexer_2 (
    .in0(soma_1_o0), .in1(\subtração_1_o0 ), .out(o0), .sel(S));  // open: in2, in3, en

  // Notes on the sheet:
  //   MAC0329 - Projeto 1
  //   Antonio Carlos Santos de Lima [8515986]
  //   Gustavo Chicato Wandeur [7557797]
  //   Victor Hugo Miranda Pinto [10297720]
endmodule

module Soma (
  input  [7:0] B,
  input  [7:0] A,
  output [7:0] S,
  output o0
);

  wire somador_de_dois_bits_1_cout, somador_de_dois_bits_2_cout, somador_de_dois_bits_3_cout,
       somador_de_dois_bits_4_cout, somador_de_dois_bits_5_cout, somador_de_dois_bits_6_cout,
       somador_de_dois_bits_7_cout, somador_de_dois_bits_8_cout;

  somador_de_dois_bits somador_de_dois_bits_1 (
    .cin(1'b0), .a(A[0]), .b(B[0]), .cout(somador_de_dois_bits_1_cout), .s(S[0]));
  somador_de_dois_bits somador_de_dois_bits_2 (
    .cin(somador_de_dois_bits_1_cout), .a(A[1]), .b(B[1]), .cout(somador_de_dois_bits_2_cout), .s(S[1]));
  somador_de_dois_bits somador_de_dois_bits_3 (
    .cin(somador_de_dois_bits_2_cout), .a(A[2]), .b(B[2]), .cout(somador_de_dois_bits_3_cout), .s(S[2]));
  somador_de_dois_bits somador_de_dois_bits_4 (
    .cin(somador_de_dois_bits_3_cout), .a(A[3]), .b(B[3]), .cout(somador_de_dois_bits_4_cout), .s(S[3]));
  somador_de_dois_bits somador_de_dois_bits_5 (
    .cin(somador_de_dois_bits_4_cout), .a(A[4]), .b(B[4]), .cout(somador_de_dois_bits_5_cout), .s(S[4]));
  somador_de_dois_bits somador_de_dois_bits_6 (
    .cin(somador_de_dois_bits_5_cout), .a(A[5]), .b(B[5]), .cout(somador_de_dois_bits_6_cout), .s(S[5]));
  somador_de_dois_bits somador_de_dois_bits_7 (
    .cin(somador_de_dois_bits_6_cout), .a(A[6]), .b(B[6]), .cout(somador_de_dois_bits_7_cout), .s(S[6]));
  somador_de_dois_bits somador_de_dois_bits_8 (
    .cin(somador_de_dois_bits_7_cout), .a(A[7]), .b(B[7]), .cout(somador_de_dois_bits_8_cout), .s(S[7]));
  xor xor_1 (o0, somador_de_dois_bits_7_cout, somador_de_dois_bits_8_cout);

  // Notes on the sheet:
  //   c0
endmodule

// +
module somador_de_dois_bits (
  input  cin,
  input  a,
  input  b,
  output cout,
  output s
);

  wire and_1_out, and_2_out, xor_1_out;

  xor xor_1 (xor_1_out, a, b);
  and and_1 (and_1_out, a, b);
  and and_2 (and_2_out, cin, xor_1_out);
  xor xor_2 (s, xor_1_out, cin);
  or or_1 (cout, and_2_out, and_1_out);
endmodule

// Sub
module \Subtração  (
  input  [7:0] A,
  input  [7:0] B,
  output [7:0] S,
  output o0
);

  wire [7:0] complemento_de_dois_1_minus_a;

  complemento_de_dois complemento_de_dois_1 (.A(B), .minus_A(complemento_de_dois_1_minus_a));
  Soma soma_1 (.A(complemento_de_dois_1_minus_a), .S(S), .o0(o0), .B(A));
endmodule

// 2C
module complemento_de_dois (
  input  [7:0] A,
  output [7:0] minus_A
);

  wire [7:0] not_1_out;

  assign not_1_out = ~A;  // NOT_Gate not_1, 8 bits wide
  Soma soma_1 (.A(8'h1), .S(minus_A), .B(not_1_out));  // open: o0
endmodule

// Comp
module Comparador (
  input  [7:0] A,
  output o1,
  output o2,
  output o3
);

  wire or_1_out, or_2_out;

  or or_1 (or_1_out, A[7], A[6], A[5], A[4], A[3], A[2], A[1], A[0]);
  not not_1 (o2, or_1_out);
  or or_2 (or_2_out, o2, A[7]);
  not not_2 (o3, or_2_out);

  assign o1 = A[7];
endmodule
