// Logisim project Projeto2.circ as structural Verilog: 8 circuits, main circuit main
module main (
  input  in_1,
  input  in_2,
  input  in_3,
  input  [1:0] in_4,
  output [15:0] out_5,
  output [15:0] out_6
);

  wire _0b, _0c, _1f, _15, _16, _29, _33, _38, _46, and_1_out, and_2_out, and_3_out, and_4_out, and_8_out,
       clock_1_out, Instru, not_1_out, not_2_out, not_3_out, not_4_out, or_1_out, or_2_out;
  wire [7:0] counter_1_q, multiplexer_1_out, multiplexer_3_out, param, PC_q, ula_1_r;
  wire [15:0] multiplexer_2_out, ram_1_data;
  wire [15:8] IR_q;

  not not_1 (not_1_out, _15);
  Multiplexer #(.width(8)) multiplexer_1 (
    .in0(counter_1_q), .in1(param), .out(multiplexer_1_out), .sel(_33), .en(Instru));
  Clock clock_1 (.out(clock_1_out));
  Multiplexer #(.width(16)) multiplexer_2 (
    .in0(ram_1_data), .in1(out_6), .out(multiplexer_2_out), .sel(_15), .en(not_1_out));
  and and_1 (and_1_out, clock_1_out, or_1_out);
  and and_2 (and_2_out, _0b, 1'b1);
  not not_2 (not_2_out, Instru);
  Register #(.width(16)) ACC (.D(multiplexer_2_out), .Q(out_5), .clk(and_1_out), .clr(in_3));  // open: en
  or or_1 (or_1_out, and_2_out, and_3_out, and_4_out);
  and and_3 (and_3_out, _15, 1'b1);
  and and_4 (and_4_out, _16, 1'b1);
  Counter counter_1 (
    .load(Instru), .D(multiplexer_1_out), .count(not_2_out), .Q(counter_1_q), .clk(clock_1_out), .clr(in_3));  // open: carry
  Counter PC (.load(Instru), .D(param), .count(1'b0), .Q(PC_q), .clk(clock_1_out), .clr(in_3));  // open: carry
  // AND_Gate and_5 has open pins: in0=_46, in1=1'b1, out=open
  // AND_Gate and_6 has open pins: in0=_1f, in1=1'b1, out=open
  // AND_Gate and_7 has open pins: in0=_29, in1=1'b1, out=open
  and and_8 (and_8_out, Instru, ~clock_1_out);  // AND_Gate
  not not_3 (not_3_out, clock_1_out);
  or or_2 (or_2_out, _0c, _1f);
  // AND_Gate and_9 has open pins: in0=_38, in1=1'b1, out=open
  // AND_Gate and_10 has open pins: in0=_0c, in1=1'b1, out=open
  Multiplexer #(.width(8)) multiplexer_3 (
    .in0(counter_1_q), .in1(PC_q), .out(multiplexer_3_out), .sel(and_8_out), .en(not_4_out));
  not not_4 (not_4_out, and_8_out);
  RAM #(.dataWidth(16), .bus("separate")) ram_1 (
    .addr(multiplexer_3_out), .din(out_5), .data(ram_1_data), .str(or_2_out), .clk(not_3_out), .ld(in_1),
    .clr(in_2));  // open: sel
  // AND_Gate and_11 has open pins: in0=_33, in1=1'b1, out=open
  Register #(.width(16)) IR (.D(ram_1_data), .Q({IR_q, param}), .clk(clock_1_out), .clr(in_3));  // open: en
  ULA ula_1 (.A(ram_1_data[15:8]), .B(out_5[15:8]), .S(in_4), .R(ula_1_r));  // open: o0, o1, o2, o3
  Seletor seletor_1 (
    .in_1(IR_q[15]), .in_2(IR_q[14]), .in_3(IR_q[13]), .in_4(IR_q[12]), .in_5(IR_q[11]), .in_6(IR_q[10]),
    .in_7(IR_q[9]), .in_8(IR_q[8]), ._0b(_0b), ._0c(_0c), ._33(_33), ._15(_15), ._38(_38), ._16(_16),
    ._46(_46), ._1f(_1f), ._29(_29));
  assign out_6 = {{8{1'b0}}, ula_1_r};  // Bit_Extender bit_extender_1
  or or_3 (Instru, _0b, _0c, _15, _38, _16, _1f, _29);

  // Other names for the same wires on the sheet: soma[15:0] = out_6

  // Notes on the sheet:
  //   MAC0329 - Projeto 2
  //   Antonio Carlos Santos de Lima [8515986]
  //   Gustavo Chicato Wandeur [7557797]
  //   Victor Hugo Miranda Pinto [10297720]
endmodule

module Seletor (
  input  in_1,
  input  in_2,
  input  in_3,
  input  in_4,
  input  in_5,
  input  in_6,
  input  in_7,
  input  in_8,
  output _0b,
  output _0c,
  output _33,
  output _15,
  output _38,
  output _16,
  output _46,
  output _1f,
  output _29
);

  and u__0c (_0c, ~in_1, ~in_2, ~in_3, ~in_4, in_5, in_6, ~in_7, ~in_8);  // AND_Gate
  and u__15 (_15, ~in_1, ~in_2, ~in_3, in_4, ~in_5, in_6, ~in_7, in_8);  // AND_Gate
  and u__16 (_16, ~in_1, ~in_2, ~in_3, in_4, ~in_5, in_6, in_7, ~in_8);  // AND_Gate
  and u__1f (_1f, ~in_1, ~in_2, ~in_3, in_4, in_5, in_6, in_7, in_8);  // AND_Gate
  and u__29 (_29, ~in_1, ~in_2, in_3, ~in_4, ~in_5, in_6, in_7, ~in_8);  // AND_Gate
  and u__0b (_0b, ~in_1, ~in_2, ~in_3, ~in_4, in_5, ~in_6, in_7, in_8);  // AND_Gate
  and u__33 (_33, ~in_1, ~in_2, in_3, in_4, ~in_5, ~in_6, in_7, in_8);  // AND_Gate
  and u__38 (_38, ~in_1, ~in_2, in_3, in_4, in_5, ~in_6, ~in_7, ~in_8);  // AND_Gate
  and u__46 (_46, ~in_1, in_2, ~in_3, ~in_4, ~in_5, in_6, in_7, ~in_8);  // AND_Gate
endmodule

module somador_de_dois_bits (
  input  cin,
  input  a,
  input  b,
  output cout,
  output s
);

  wire and_1_out, and_2_out, xor_1_out;

  xor xor_1 (xor_1_out, a, b);
  and and_1 (and_1_out, a, b);
  and and_2 (and_2_out, cin, xor_1_out);
  xor xor_2 (s, xor_1_out, cin);
  or or_1 (cout, and_2_out, and_1_out);
endmodule

module Soma (
  input  [7:0] B,
  input  [7:0] A,
  output [7:0] S,
  output o0
);

  wire somador_de_dois_bits_1_cout, somador_de_dois_bits_2_cout, somador_de_dois_bits_3_cout,
       somador_de_dois_bits_4_cout, somador_de_dois_bits_5_cout, somador_de_dois_bits_6_cout,
       somador_de_dois_bits_7_cout, somador_de_dois_bits_8_cout;

  somador_de_dois_bits somador_de_dois_bits_1 (
    .cin(1'b0), .a(A[0]), .b(B[0]), .cout(somador_de_dois_bits_1_cout), .s(S[0]));
  somador_de_dois_bits somador_de_dois_bits_2 (
    .cin(somador_de_dois_bits_1_cout), .a(A[1]), .b(B[1]), .cout(somador_de_dois_bits_2_cout), .s(S[1]));
  somador_de_dois_bits somador_de_dois_bits_3 (
    .cin(somador_de_dois_bits_2_cout), .a(A[2]), .b(B[2]), .cout(somador_de_dois_bits_3_cout), .s(S[2]));
  somador_de_dois_bits somador_de_dois_bits_4 (
    .cin(somador_de_dois_bits_3_cout), .a(A[3]), .b(B[3]), .cout(somador_de_dois_bits_4_cout), .s(S[3]));
  somador_de_dois_bits somador_de_dois_bits_5 (
    .cin(somador_de_dois_bits_4_cout), .a(A[4]), .b(B[4]), .cout(somador_de_dois_bits_5_cout), .s(S[4]));
  somador_de_dois_bits somador_de_dois_bits_6 (
    .cin(somador_de_dois_bits_5_cout), .a(A[5]), .b(B[5]), .cout(somador_de_dois_bits_6_cout), .s(S[5]));
  somador_de_dois_bits somador_de_dois_bits_7 (
    .cin(somador_de_dois_bits_6_cout), .a(A[6]), .b(B[6]), .cout(somador_de_dois_bits_7_cout), .s(S[6]));
  somador_de_dois_bits somador_de_dois_bits_8 (
    .cin(somador_de_dois_bits_7_cout), .a(A[7]), .b(B[7]), .cout(somador_de_dois_bits_8_cout), .s(S[7]));
  xor xor_1 (o0, somador_de_dois_bits_7_cout, somador_de_dois_bits_8_cout);

  // Notes on the sheet:
  //   c0
endmodule

module complemento_de_dois (
  input  [7:0] A,
  output [7:0] minus_A
);

  wire [7:0] not_1_out;

  assign not_1_out = ~A;  // NOT_Gate not_1, 8 bits wide
  Soma soma_1 (.A(not_1_out), .S(minus_A), .B(8'h1));  // open: o0
endmodule

module \Subtração  (
  input  [7:0] A,
  input  [7:0] B,
  output [7:0] S,
  output o0
);

  wire [7:0] complemento_de_dois_1_minus_a;

  complemento_de_dois complemento_de_dois_1 (.A(B), .minus_A(complemento_de_dois_1_minus_a));
  Soma soma_1 (.A(A), .S(S), .o0(o0), .B(complemento_de_dois_1_minus_a));
endmodule

module Comparador (
  input  [7:0] A,
  output o1,
  output o2,
  output o3
);

  wire or_1_out, or_2_out;

  or or_1 (or_1_out, A[7], A[6], A[5], A[4], A[3], A[2], A[1], A[0]);
  not not_1 (o2, or_1_out);
  or or_2 (or_2_out, o2, A[7]);
  not not_2 (o3, or_2_out);

  assign o1 = A[7];
endmodule

module ULA (
  input  [7:0] A,
  input  [7:0] B,
  input  [1:0] S,
  output [7:0] R,
  output o0,
  output o1,
  output o2,
  output o3
);

  wire soma_1_o0, \subtração_1_o0 ;
  wire [7:0] soma_1_s, \subtração_1_s ;

  Comparador comparador_1 (.A(A), .o1(o3), .o2(o2), .o3(o1));
  Soma soma_1 (.A(A), .S(soma_1_s), .o0(soma_1_o0), .B(B));
  \Subtração  \subtração_1  (.A(A), .B(B), .S(\subtração_1_s ), .o0(\subtração_1_o0 ));
  Multiplexer #(.select(2), .width(8)) multiplexer_1 (
    .in0(soma_1_s), .in1(\subtração_1_s ), .out(R), .sel(S));  // open: in2, in3, en
  Multiplexer #(.select(2)) multiplexer_2 (
    .in0(soma_1_o0), .in1(\subtração_1_o0 ), .out(o0), .sel(S));  // open: in2, in3, en
endmodule
