// Logisim project ram.circ as structural Verilog: 1 circuit, main circuit main
// write=0/qread=1
module main (
  input  [15:0] in_1,
  input  inc_1,
  input  reset_1,
  input  write_0_read_1,
  input  _0__destino_0___1__destino_1
);

  wire clock_1_out, not_1_out;
  wire [7:0] contador_de_8_bits_q;
  wire [15:0] demultiplexer_1_out0, demultiplexer_1_out1, ram_1_data;

  Clock clock_1 (.out(clock_1_out));
  Counter contador_de_8_bits (
    .count(inc_1), .Q(contador_de_8_bits_q), .clk(clock_1_out), .clr(reset_1));  // open: load, D, carry
  RAM #(.dataWidth(16)) ram_1 (
    .addr(contador_de_8_bits_q), .data(ram_1_data), .clk(clock_1_out), .ld(write_0_read_1));  // open: sel, clr
  not not_1 (not_1_out, write_0_read_1);
  assign ram_1_data = not_1_out ? in_1 : 16'bz;  // Controlled_Buffer controlled_buffer_1
  Demultiplexer #(.width(16)) demultiplexer_1 (
    .out0(demultiplexer_1_out0), .out1(demultiplexer_1_out1), .in(ram_1_data),
    .sel(_0__destino_0___1__destino_1));  // open: en
  Hex_Digit_Display hex_digit_display_1 (.value(demultiplexer_1_out0[11:8]));  // open: dp
  Hex_Digit_Display hex_digit_display_2 (.value(demultiplexer_1_out0[15:12]));  // open: dp
  Hex_Digit_Display hex_digit_display_3 (.value(demultiplexer_1_out1[15:12]));  // open: dp
  Hex_Digit_Display hex_digit_display_4 (.value(demultiplexer_1_out1[11:8]));  // open: dp
  Hex_Digit_Display hex_digit_display_5 (.value(demultiplexer_1_out0[7:4]));  // open: dp
  Hex_Digit_Display hex_digit_display_6 (.value(demultiplexer_1_out1[7:4]));  // open: dp
  Hex_Digit_Display hex_digit_display_7 (.value(demultiplexer_1_out0[3:0]));  // open: dp
  Hex_Digit_Display hex_digit_display_8 (.value(demultiplexer_1_out1[3:0]));  // open: dp

  // Notes on the sheet:
  //   input
  //   destino 0
  //   destino 1
endmodule
